# Fritzing sketch M5_Stack (saved by Fritzing 1.0.0rc)

parts:
  Mod1 = Raspberry Pi Pico W
  M5Stack1 = M5Stack LoRaWAN ASR6501 868 MHz [package="Grove connector"]

nets:
  N1: Mod1.pin_1, M5Stack1.RXD
  N2: Mod1.pin_2, M5Stack1.TXD
  N3: Mod1.pin_36, M5Stack1.5V
  N4: Mod1.pin_38, Mod1.pin_42, M5Stack1.GND

notes:
  Your Sensor might differ from the one shown here. Ask a TA if you are unsure of how to connect.

custom parts:
  Raspberry Pi Pico W: Raspberry Pi Pico W. Based around the RP2040 microcontroller the Pico W is a low cost microcontroller device bringing Raspberry Pi quality, cost, and easy of use to the microcontroller space. The areas marked KEEPOUT in pcb silkscreen should not have traces running through them to avoid shorts on a soldered in module!
  M5Stack LoRaWAN ASR6501 868 MHz: Unit LoRaWAN868 is a LoRaWAN communication module suitable for 868MHz frequency launched by M5Stack. The module adopts the ASR6501 scheme, which supports long-distance communication and has both ultra-low power consumption and high sensitivity. The module integrates the LoRaWAN protocol stack and adopts a serial communication interface (using the AT command set for control). When used, it can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
