# Fritzing sketch Reed_Switch (saved by Fritzing 1.0.0rc)
breadboards: 1

parts:
  Mod1 = Raspberry Pi Pico W
  Part3 = KY-021 Mini Magnetic Reed Switch Module [package="Breakout board"]

nets:
  N1: Mod1.pin_32, Part3.-
  N2: Mod1.pin_36, Part3.S
  N3: Mod1.pin_38, Mod1.pin_42, Part3.Vin

notes:
  Your Sensor might differ from the one shown here. Ask a TA if you are unsure of how to connect.

custom parts:
  Raspberry Pi Pico W: Raspberry Pi Pico W. Based around the RP2040 microcontroller the Pico W is a low cost microcontroller device bringing Raspberry Pi quality, cost, and easy of use to the microcontroller space. The areas marked KEEPOUT in pcb silkscreen should not have traces running through them to avoid shorts on a soldered in module!
  KY-021 Mini Magnetic Reed Switch Module: KY-021 magnetic reed switch module. A reed switch is a magnetic sensor that is normally open and gets closed when exposed to a magnetic field.
