# Fritzing sketch Hall_Sensor_Digital_Analog (saved by Fritzing 1.0.0rc)
breadboards: 1

parts:
  Mod1 = Raspberry Pi Pico W
  Part4 = KY-003 Hall Magnetic Sensor Module [package="Breakout board"]

nets:
  N1: Mod1.pin_32, Part4.S
  N2: Mod1.pin_36, Part4.Vin
  N3: Mod1.pin_38, Mod1.pin_42, Part4.-

notes:
  Your Sensor might differ from the one shown here. Ask a TA if you are unsure of how to connect.

custom parts:
  Raspberry Pi Pico W: Raspberry Pi Pico W. Based around the RP2040 microcontroller the Pico W is a low cost microcontroller device bringing Raspberry Pi quality, cost, and easy of use to the microcontroller space. The areas marked KEEPOUT in pcb silkscreen should not have traces running through them to avoid shorts on a soldered in module!
  KY-003 Hall Magnetic Sensor Module: KEYES KY-003 Arduino Hall Magnetic Sensor Module is a switch that will turn on/off in the presence of a magnetic field.
