# Fritzing sketch Hall_Sensor_Digital_Analog_with_resistor (saved by Fritzing 1.0.0rc)
breadboards: 1

parts:
  Mod1 = Raspberry Pi Pico W
  S1 = Hall Sensor [part_number=WSH130 package=TO92]
  R1 = Resistor [tolerance=±5% resistance=4.7 package="0805 [SMD]"]

nets:
  N1: Mod1.pin_32, S1.OUT, R1.Pin_0
  N2: Mod1.pin_36, S1.VCC, R1.Pin_1
  N3: Mod1.pin_38, Mod1.pin_42, S1.GND

notes:
  Your Sensor might differ from the one shown here. Ask a TA if you are unsure of how to connect.
  4.7 Kohm

custom parts:
  Raspberry Pi Pico W: Raspberry Pi Pico W. Based around the RP2040 microcontroller the Pico W is a low cost microcontroller device bringing Raspberry Pi quality, cost, and easy of use to the microcontroller space. The areas marked KEEPOUT in pcb silkscreen should not have traces running through them to avoid shorts on a soldered in module!
  Hall Sensor: A Hall Sensor
