# Fritzing sketch Active_Piezo_Buzzer (saved by Fritzing 1.0.0rc)
breadboards: 1

parts:
  Mod1 = Raspberry Pi Pico W
  A1 = KY-039 [package=THT]

nets:
  N1: Mod1.pin_32, A1.pin1
  N2: Mod1.pin_36, A1.pin2
  N3: Mod1.pin_38, Mod1.pin_42, A1.pin3

notes:
  Your Sensor might differ from the one shown here. Ask a TA if you are unsure of how to connect.

custom parts:
  Raspberry Pi Pico W: Raspberry Pi Pico W. Based around the RP2040 microcontroller the Pico W is a low cost microcontroller device bringing Raspberry Pi quality, cost, and easy of use to the microcontroller space. The areas marked KEEPOUT in pcb silkscreen should not have traces running through them to avoid shorts on a soldered in module!
  KY-039: KY-039 heart beat sensor.
