# Fritzing sketch LDR_Photo_Resistor_47 (saved by Fritzing 1.0.0rc)
breadboards: 1

parts:
  Mod1 = Raspberry Pi Pico W
  R1 = Photocell (LDR) [power=0.25W dark_resistance_@0.01lx=300kΩ light_resistance_@100lx=400Ω luminance=10lx package=THT]
  R2 = Resistor [tolerance=±5% resistance=4.7k package="0805 [SMD]"]

nets:
  N1: Mod1.pin_32, R1.pin_0, R2.Pin_1
  N2: Mod1.pin_36, R2.Pin_0
  N3: Mod1.pin_38, Mod1.pin_42, R1.pin_1

notes:
  Your Sensor might differ from the one shown here. Ask a TA if you are unsure of how to connect.
  4.7 Kohm

custom parts:
  Raspberry Pi Pico W: Raspberry Pi Pico W. Based around the RP2040 microcontroller the Pico W is a low cost microcontroller device bringing Raspberry Pi quality, cost, and easy of use to the microcontroller space. The areas marked KEEPOUT in pcb silkscreen should not have traces running through them to avoid shorts on a soldered in module!
