# Fritzing sketch Small_Microphone (saved by Fritzing 1.0.0rc)
breadboards: 1

parts:
  Mod1 = Raspberry Pi Pico W
  KY-1 = KY-038 Sound Sensor Module [package="Breakout board"]

nets:
  N1: Mod1.pin_31, KY-1.D0
  N2: Mod1.pin_36, KY-1.+
  N3: Mod1.pin_38, Mod1.pin_42, KY-1.G

notes:
  Your Sensor might differ from the one shown here. Ask a TA if you are unsure of how to connect.

custom parts:
  Raspberry Pi Pico W: Raspberry Pi Pico W. Based around the RP2040 microcontroller the Pico W is a low cost microcontroller device bringing Raspberry Pi quality, cost, and easy of use to the microcontroller space. The areas marked KEEPOUT in pcb silkscreen should not have traces running through them to avoid shorts on a soldered in module!
  KY-038 Sound Sensor Module: Microphone Sound Sensor. It reacts on specific sound volume. Digital and analog Output.
