# Fritzing sketch MCP9700 (saved by Fritzing 1.0.0rc)
breadboards: 1

parts:
  Mod1 = Raspberry Pi Pico W
  T1 = MCP9700-E/TO Temperature Sensor [package="TO92 [THT]"]

nets:
  N1: Mod1.pin_32, T1.Vout
  N2: Mod1.pin_36, T1.+Vs
  N3: Mod1.pin_38, Mod1.pin_42, T1.GND

notes:
  Your Sensor might differ from the one shown here. Ask a TA if you are unsure of how to connect.

custom parts:
  Raspberry Pi Pico W: Raspberry Pi Pico W. Based around the RP2040 microcontroller the Pico W is a low cost microcontroller device bringing Raspberry Pi quality, cost, and easy of use to the microcontroller space. The areas marked KEEPOUT in pcb silkscreen should not have traces running through them to avoid shorts on a soldered in module!
  MCP9700-E/TO Temperature Sensor: A MCP9700-E/TO temperature sensor with a temperature range from -40°C to 125°C.
