# Fritzing sketch Soil_Moisture (saved by Fritzing 1.0.0rc)
breadboards: 1

parts:
  Mod1 = Raspberry Pi Pico W
  부품4 = FC-28 Soil Hygrometer Module - Probe
  Part1 = FC-28 Soil Hygrometer Module

nets:
  N1: Mod1.pin_32, Part1.AO
  N2: Mod1.pin_36, Part1.VCC
  N3: Mod1.pin_38, Mod1.pin_42, Part1.GND
  N4: 부품4.POS, Part1.POS
  N5: 부품4.NEG, Part1.NEG

notes:
  Your Sensor might differ from the one shown here. Ask a TA if you are unsure of how to connect.

custom parts:
  Raspberry Pi Pico W: Raspberry Pi Pico W. Based around the RP2040 microcontroller the Pico W is a low cost microcontroller device bringing Raspberry Pi quality, cost, and easy of use to the microcontroller space. The areas marked KEEPOUT in pcb silkscreen should not have traces running through them to avoid shorts on a soldered in module!
  FC-28 Soil Hygrometer Module - Probe: The FC-28 is a soil hygrometer module that uses the Texas Instruments LM393 comparator chip to provide an analog measurement of soil humidity.
  FC-28 Soil Hygrometer Module: The FC-28 is a soil hygrometer module that uses the Texas Instruments LM393 comparator chip to provide an analog measurement of soil humidity. The digital output is high when soil moisture is over a certain threshold, as determined by adjusting the potentiometer.
