# Fritzing sketch DHT11_Resistor (saved by Fritzing 1.0.0rc)
breadboards: 1

parts:
  Mod1 = Raspberry Pi Pico W
  DHT2 = Humidity and Temperature Sensor DHT11
  R1 = Resistor [tolerance=±5% resistance=4.7k package="0603 [SMD]"]

nets:
  N1: Mod1.pin_32, DHT2.Data-signal, R1.Pin_0
  N2: Mod1.pin_36, DHT2.Vcc, R1.Pin_1
  N3: Mod1.pin_38, Mod1.pin_42, DHT2.GND_2

notes:
  Your Sensor might differ from the one shown here. Ask a TA if you are unsure of how to connect.
  4.7 Kohm resistor

custom parts:
  Raspberry Pi Pico W: Raspberry Pi Pico W. Based around the RP2040 microcontroller the Pico W is a low cost microcontroller device bringing Raspberry Pi quality, cost, and easy of use to the microcontroller space. The areas marked KEEPOUT in pcb silkscreen should not have traces running through them to avoid shorts on a soldered in module!
  Humidity and Temperature Sensor DHT11: Digital relative humidity & temperature sensor DHT11
