# Fritzing sketch Two_Color_LED (saved by Fritzing 1.0.0rc)
breadboards: 1

parts:
  Mod1 = Raspberry Pi Pico W
  Mod2 = KY-011 Two Color LED Module [package="Breakout board"]

nets:
  N1: Mod1.pin_31, Mod2.-
  N2: Mod1.pin_32, Mod2.Vin
  N3: Mod1.pin_38, Mod1.pin_42, Mod2.S

notes:
  Your Sensor might differ from the one shown here. Ask a TA if you are unsure of how to connect.

custom parts:
  Raspberry Pi Pico W: Raspberry Pi Pico W. Based around the RP2040 microcontroller the Pico W is a low cost microcontroller device bringing Raspberry Pi quality, cost, and easy of use to the microcontroller space. The areas marked KEEPOUT in pcb silkscreen should not have traces running through them to avoid shorts on a soldered in module!
  KY-011 Two Color LED Module: KY-011 Two Color LED Module consist of a common cathode 3mm red/green LED.
